# Fritzing sketch wirelessnetworkv3 (saved by Fritzing 0.8.7b)
breadboards: 2

parts:
  Raspberry_Pi_rev2 = Raspberry Pi B rev2
  Part5 = Arduino Nano (Rev3.0)
  U3 = RF-LINK_RX [package=rf-link_rx]
  Part6 = Logic Level Converter
  J2 = Power Jack [package=power_jack_smd]  # not connected
  J3 = Power Jack [package=power_jack_smd]  # not connected
  Part7 = Arduino Nano (Rev3.0)
  U4 = RF-LINK_TX [package=rf-link_tx]
  RHT3 = Humidity and Temperature Sensor RHT03
  R3 = Resistor [tolerance=±5% resistance=1k package=THT]
  J4 = Power Jack [package=power_jack_pth_lock]
  J5 = Power Jack [package=power_jack_smd]  # not connected
  J6 = Power Jack [package=power_jack_smd]  # not connected

nets:
  N1: Raspberry_Pi_rev2.3V3, Part6.LV
  5V: Raspberry_Pi_rev2.5V, Part5.VIN, U3.+5V, Part6.HV
  GND: Raspberry_Pi_rev2.GND, Part5.GND, U3.GND, Part6.GND
  N2: Raspberry_Pi_rev2.GPIO_14, Part6.RX_LV
  N3: Raspberry_Pi_rev2.GPIO_15, Part6.TX_LV
  N4: Part5.D1/TX, Part6.TX_HV
  N5: Part5.D0/RX, Part6.RX_HV
  N6: Part5.D2, U3.DATA
  GND_2: Part7.GND, U4.GND, RHT3.GND_2, J4.GND
  N7: Part7.D3, U4.DATA
  N8: Part7.D4, RHT3.Data-signal, R3.Pin_1
  N9: Part7.VIN, J4.PWR
  5V_2: Part7.5V, U4.+5V, RHT3.Vcc, R3.Pin_0

notes:
  5v to components
  Sensor
  Transmitter,
  6.5" antenna
  3.3v to 5v
  logic level
  converter
  6.5" Wire Antenna
  Receiver
  Arduino
  9v to arduino
